// Logisim project Project_1.circ as structural Verilog: 2 circuits, main circuit main
module main (
  input  A,
  input  B,
  input  C
);

  wire and_1_out, and_2_out, and_3_out, and_4_out, and_5_out, not_1_out, not_2_out, not_3_out, or_1_out;

  not not_1 (not_1_out, A);
  not not_2 (not_2_out, B);
  not not_3 (not_3_out, C);
  and and_1 (and_1_out, A, B, C);
  and and_2 (and_2_out, not_1_out, B, C);
  and and_3 (and_3_out, A, not_2_out, not_3_out);
  and and_4 (and_4_out, A, not_2_out, C);
  and and_5 (and_5_out, not_1_out, not_2_out, C);
  or or_1 (or_1_out, and_1_out, and_2_out, and_3_out, and_4_out, and_5_out);
  LED led_1 (.in(or_1_out));
endmodule

module NAND_Version (
  input  A,
  input  B,
  input  C
);

  wire nand_1_out, nand_2_out, nand_3_out, nand_4_out, nand_5_out, nand_6_out, nand_7_out, nand_8_out,
       nand_9_out;

  nand nand_1 (nand_1_out, A, A);
  nand nand_2 (nand_2_out, B, B);
  nand nand_3 (nand_3_out, C, C);
  nand nand_4 (nand_4_out, A, B, C);
  nand nand_5 (nand_5_out, nand_1_out, B, C);
  nand nand_6 (nand_6_out, A, nand_2_out, nand_3_out);
  nand nand_7 (nand_7_out, A, nand_2_out, C);
  nand nand_8 (nand_8_out, nand_1_out, nand_2_out, C);
  nand nand_9 (nand_9_out, nand_4_out, nand_5_out, nand_6_out, nand_7_out, nand_8_out);
  LED led_1 (.in(nand_9_out));
endmodule
